// Digital circuit frontpanel.dig as structural Verilog
module frontpanel (
  input  [15:0] value_2,
  input  [1:0] dest,
  input  [1:0] src,
  output [15:0] R0,
  output [15:0] R1,
  output [15:0] R2,
  output [15:0] R3,
  output [15:0] B,
  output [1:0] rs,
  output [1:0] rd,
  output [15:0] value,
  output [3:0] PC,
  output [15:0] value_3
);

  wire add, add_out, advance_out, assembler_1_store_clk, execute_1_p4, fetch_1_p8, jump, jump_out, mode_out,
       pmshim_1_c, pmshim_1_l, pmshim_1_s;
  wire [3:0] pmshim_1_a;
  wire [31:0] assembler_1_inst, pmshim_1_d, Program_d;

  LED programming (.in(mode_out));
  DipSwitch mode (.out(mode_out));
  Button u_add (.out(add_out));
  Button u_jump (.out(jump_out));
  assembler assembler_1 (
    .mode(mode_out), .value(value_2), .dest(dest), .src(src), .add(add_out), .jump(jump_out),
    .inst(assembler_1_inst), .store_clk(assembler_1_store_clk));
  pmshim pmshim_1 (
    .pc(PC), .i_in(assembler_1_inst), .s_c(assembler_1_store_clk), .A(pmshim_1_a), .D(pmshim_1_d),
    .s(pmshim_1_s), .C(pmshim_1_c), .L(pmshim_1_l));
  EEPROMDualPort #(.AddrBits(4), .isProgramMemory("true"), .Bits(32)) Program (
    .A(pmshim_1_a), .Din(pmshim_1_d), .str(pmshim_1_s), .C(pmshim_1_c), .ld(pmshim_1_l), .D(Program_d));
  Button advance (.out(advance_out));
  LED jump_2 (.in(jump));
  LED add_2 (.in(add));
  // fetch fetch_1: pin names not known; wires that end beside it: mode_out, assembler_1_inst, Program_d, advance_out, value, jump, PC, fetch_1_p8
  // decoder decoder_1: pin names not known; wires that end beside it: fetch_1_p8, rs, rd, add, value, jump
  // execute execute_1: pin names not known; wires that end beside it: add, value, B, execute_1_p4
  // regfile regfile_1: pin names not known; wires that end beside it: rs, rd, execute_1_p4, advance_out, R0, R1, R2, R3, B

  assign value_3 = value;

  // Other names for the same wires on the sheet: V[15:0] = value

  // Notes on the sheet:
  //   contents of Program (hex, n*v repeats v):
  //   64,100c8,120063,230022,30002a,7000001
  //   PC =
  //   =
  //   R
  //   +
  //   ( R
  //   )
endmodule
